// Logisim project 1.circ as structural Verilog: 3 circuits, main circuit 1
module _1 (
  input  x,
  output out_2
);

  wire clock_1_out;

  Clock clock_1 (.out(clock_1_out));
  J_K_Flip_Flop j_k_ff_1 (.J(x), .clk(clock_1_out), .K(x), .Q(out_2));  // open: Qn, preset, en, reset
endmodule

module _2 (
  input  x
);

  wire A_q, A_qn, and_1_out, and_2_out, and_3_out, B_q, C_q, clock_1_out, not_1_out, or_1_out, or_2_out,
       or_3_out;

  Clock clock_1 (.out(clock_1_out));
  and and_1 (and_1_out, not_1_out, C_q, B_q);
  J_K_Flip_Flop A (.J(and_1_out), .clk(clock_1_out), .K(1'b0), .Q(A_q), .Qn(A_qn));  // open: preset, en, reset
  not not_1 (not_1_out, x);
  and and_2 (and_2_out, C_q, x);
  or or_1 (or_1_out, C_q, not_1_out);
  J_K_Flip_Flop B (.J(and_2_out), .clk(clock_1_out), .K(or_1_out), .Q(B_q));  // open: Qn, preset, en, reset
  or or_2 (or_2_out, B_q, and_3_out);
  or or_3 (or_3_out, x, A_q);
  and and_3 (and_3_out, not_1_out, A_qn);
  J_K_Flip_Flop C (.J(or_2_out), .clk(clock_1_out), .K(or_3_out), .Q(C_q));  // open: Qn, preset, en, reset
endmodule

module _3 (
  input  x
);

  wire A_q, A_qn, and_1_out, and_2_out, and_3_out, and_4_out, B_q, B_qn, C_q, C_qn, clock_1_out, not_1_out,
       not_2_out, or_1_out, or_2_out, or_3_out, xor_1_out, xor_2_out;

  Clock clock_1 (.out(clock_1_out));
  or or_1 (or_1_out, xor_1_out, B_q);
  J_K_Flip_Flop A (.J(or_1_out), .clk(clock_1_out), .K(1'b1), .Q(A_q), .Qn(A_qn));  // open: preset, en, reset
  not not_1 (not_1_out, x);
  xor xor_1 (xor_1_out, x, C_q);
  or or_2 (or_2_out, and_1_out, and_2_out);
  and and_1 (and_1_out, A_q, not_1_out);
  and and_2 (and_2_out, x, C_qn);
  xor xor_2 (xor_2_out, A_q, x);
  J_K_Flip_Flop B (.J(or_2_out), .clk(clock_1_out), .K(xor_2_out), .Q(B_q), .Qn(B_qn));  // open: preset, en, reset
  and and_3 (and_3_out, x, A_qn, B_qn);
  not not_2 (not_2_out, x);
  and and_4 (and_4_out, not_2_out, A_q, B_q);
  J_K_Flip_Flop C (.J(1'b1), .clk(clock_1_out), .K(or_3_out), .Q(C_q), .Qn(C_qn));  // open: preset, en, reset
  or or_3 (or_3_out, and_3_out, and_4_out);
endmodule
