// Logisim project 4.circ as structural Verilog: 1 circuit, main circuit main
module main (
);

  wire A_q, A_qn, and_1_out, B_q, B_qn, C_qn, clock_1_out, or_1_out;

  and and_1 (and_1_out, B_q, A_q);
  Clock clock_1 (.out(clock_1_out));
  J_K_Flip_Flop C (.J(B_qn), .clk(clock_1_out), .K(and_1_out), .Qn(C_qn));  // open: Q, preset, en, reset
  or or_1 (or_1_out, C_qn, A_qn);
  J_K_Flip_Flop B (.J(1'b1), .clk(clock_1_out), .K(or_1_out), .Q(B_q), .Qn(B_qn));  // open: preset, en, reset
  J_K_Flip_Flop A (.J(B_q), .clk(clock_1_out), .K(C_qn), .Q(A_q), .Qn(A_qn));  // open: preset, en, reset
endmodule
