// Logisim project 8-1 mux.circ as structural Verilog: 3 circuits, main circuit 2-1 mux
module _2_1_mux (
  input  x,
  input  y,
  input  s,
  output out_4
);

  wire and_1_out, and_2_out, not_1_out;

  not not_1 (not_1_out, s);
  and and_1 (and_1_out, x, not_1_out);
  and and_2 (and_2_out, y, s);
  or or_1 (out_4, and_1_out, and_2_out);
endmodule

module _4_1_mux (
  input  x,
  input  y,
  input  z,
  input  t,
  input  s1,
  input  s2,
  output out_7
);

  wire n2_1_mux_1_out_4, n2_1_mux_2_out_4;

  _2_1_mux u_2_1_mux_1 (.x(x), .y(y), .s(s1), .out_4(n2_1_mux_1_out_4));
  _2_1_mux u_2_1_mux_2 (.x(z), .y(t), .s(s1), .out_4(n2_1_mux_2_out_4));
  _2_1_mux u_2_1_mux_3 (.x(n2_1_mux_1_out_4), .y(n2_1_mux_2_out_4), .s(s2), .out_4(out_7));
endmodule

module _8_1_mux (
  input  x,
  input  in_2,
  input  in_3,
  input  in_4,
  input  in_5,
  input  in_6,
  input  in_7,
  input  in_8,
  input  in_9,
  input  in_10,
  input  in_11,
  output out_12
);

  wire n4_1_mux_1_out_7, n4_1_mux_2_out_7;

  _4_1_mux u_4_1_mux_1 (.x(x), .y(in_2), .z(in_3), .t(in_4), .s1(in_9), .s2(in_10), .out_7(n4_1_mux_1_out_7));
  _4_1_mux u_4_1_mux_2 (.x(in_5), .y(in_6), .z(in_7), .t(in_8), .s1(in_9), .s2(in_10), .out_7(n4_1_mux_2_out_7));
  _2_1_mux u_2_1_mux_1 (.x(n4_1_mux_1_out_7), .y(n4_1_mux_2_out_7), .s(in_11), .out_4(out_12));
endmodule
