// Logisim project serijski ulaz.circ as structural Verilog: 1 circuit, main circuit pomeracki registar sa serijskim ulazom
module pomeracki_registar_sa_serijskim_ulazom (
  input  in_1,
  input  S_in,
  output S_out
);

  wire d_ff_1_q, d_ff_2_q, d_ff_3_q;

  D_Flip_Flop d_ff_1 (.clk(in_1), .D(S_in), .Q(d_ff_1_q));  // open: Qn, preset, en, reset
  D_Flip_Flop d_ff_2 (.clk(in_1), .D(d_ff_1_q), .Q(d_ff_2_q));  // open: Qn, preset, en, reset
  D_Flip_Flop d_ff_3 (.clk(in_1), .D(d_ff_2_q), .Q(d_ff_3_q));  // open: Qn, preset, en, reset
  D_Flip_Flop d_ff_4 (.clk(in_1), .D(d_ff_3_q), .Q(S_out));  // open: Qn, preset, en, reset
endmodule
