// Logisim project zadatak sa 4 opcije.circ as structural Verilog: 1 circuit, main circuit zadatak sa 4 opcije
module zadatak_sa_4_opcije (
  input  x3,
  input  x2,
  input  x1,
  input  x0,
  input  [1:0] in_5,
  output out_6,
  output out_7,
  output out_8,
  output out_9
);

  Multiplexer #(.select(2)) multiplexer_1 (
    .in0(1'b0), .in1(x1), .in2(x2), .in3(x0), .out(out_6), .sel(in_5));  // open: en
  Multiplexer #(.select(2)) multiplexer_2 (
    .in0(x3), .in1(x0), .in2(x1), .in3(x3), .out(out_7), .sel(in_5));  // open: en
  Multiplexer #(.select(2)) multiplexer_3 (
    .in0(x2), .in1(x0), .in2(x0), .in3(x2), .out(out_8), .sel(in_5));  // open: en
  Multiplexer #(.select(2)) multiplexer_4 (
    .in0(x1), .in1(x0), .in2(1'b0), .in3(x1), .out(out_9), .sel(in_5));  // open: en
endmodule
