// Logisim project shift u desno.circ as structural Verilog: 1 circuit, main circuit shift u desno
module shift_u_desno (
  input  x7,
  input  x6,
  input  x5,
  input  x4,
  input  x3,
  input  x2,
  input  x1,
  input  x0,
  input  s1,
  input  s2,
  input  s3,
  output out_12,
  output out_13,
  output out_14,
  output out_15,
  output out_16,
  output out_17,
  output out_18,
  output out_19
);

  wire multiplexer_1_out, multiplexer_2_out, multiplexer_3_out, multiplexer_4_out, multiplexer_5_out,
       multiplexer_6_out, multiplexer_7_out, multiplexer_8_out, multiplexer_9_out, multiplexer_10_out,
       multiplexer_11_out, multiplexer_12_out, multiplexer_13_out, multiplexer_14_out, multiplexer_15_out,
       multiplexer_16_out;

  Multiplexer multiplexer_1 (.in0(x7), .in1(x3), .out(multiplexer_1_out), .sel(s1));  // open: en
  Multiplexer multiplexer_2 (.in0(x6), .in1(x2), .out(multiplexer_2_out), .sel(s1));  // open: en
  Multiplexer multiplexer_3 (.in0(x5), .in1(x1), .out(multiplexer_3_out), .sel(s1));  // open: en
  Multiplexer multiplexer_4 (.in0(x4), .in1(x0), .out(multiplexer_4_out), .sel(s1));  // open: en
  Multiplexer multiplexer_5 (.in0(x3), .in1(1'b0), .out(multiplexer_5_out), .sel(s1));  // open: en
  Multiplexer multiplexer_6 (.in0(x2), .in1(1'b0), .out(multiplexer_6_out), .sel(s1));  // open: en
  Multiplexer multiplexer_7 (.in0(x1), .in1(1'b0), .out(multiplexer_7_out), .sel(s1));  // open: en
  Multiplexer multiplexer_8 (.in0(x0), .in1(1'b0), .out(multiplexer_8_out), .sel(s1));  // open: en
  Multiplexer multiplexer_9 (
    .in0(multiplexer_1_out), .in1(multiplexer_3_out), .out(multiplexer_9_out), .sel(s2));  // open: en
  Multiplexer multiplexer_10 (
    .in0(multiplexer_2_out), .in1(multiplexer_4_out), .out(multiplexer_10_out), .sel(s2));  // open: en
  Multiplexer multiplexer_11 (
    .in0(multiplexer_3_out), .in1(multiplexer_5_out), .out(multiplexer_11_out), .sel(s2));  // open: en
  Multiplexer multiplexer_12 (
    .in0(multiplexer_4_out), .in1(multiplexer_6_out), .out(multiplexer_12_out), .sel(s2));  // open: en
  Multiplexer multiplexer_13 (
    .in0(multiplexer_5_out), .in1(multiplexer_7_out), .out(multiplexer_13_out), .sel(s2));  // open: en
  Multiplexer multiplexer_14 (
    .in0(multiplexer_6_out), .in1(multiplexer_8_out), .out(multiplexer_14_out), .sel(s2));  // open: en
  Multiplexer multiplexer_15 (.in0(multiplexer_7_out), .in1(1'b0), .out(multiplexer_15_out), .sel(s2));  // open: en
  Multiplexer multiplexer_16 (.in0(multiplexer_8_out), .in1(1'b0), .out(multiplexer_16_out), .sel(s2));  // open: en
  Multiplexer multiplexer_17 (.in0(multiplexer_9_out), .in1(multiplexer_10_out), .out(out_12), .sel(s3));  // open: en
  Multiplexer multiplexer_18 (.in0(multiplexer_10_out), .in1(multiplexer_11_out), .out(out_13), .sel(s3));  // open: en
  Multiplexer multiplexer_19 (.in0(multiplexer_11_out), .in1(multiplexer_12_out), .out(out_14), .sel(s3));  // open: en
  Multiplexer multiplexer_20 (.in0(multiplexer_12_out), .in1(multiplexer_13_out), .out(out_15), .sel(s3));  // open: en
  Multiplexer multiplexer_21 (.in0(multiplexer_13_out), .in1(multiplexer_14_out), .out(out_16), .sel(s3));  // open: en
  Multiplexer multiplexer_22 (.in0(multiplexer_14_out), .in1(multiplexer_15_out), .out(out_17), .sel(s3));  // open: en
  Multiplexer multiplexer_23 (.in0(multiplexer_15_out), .in1(multiplexer_16_out), .out(out_18), .sel(s3));  // open: en
  Multiplexer multiplexer_24 (.in0(multiplexer_16_out), .in1(1'b0), .out(out_19), .sel(s3));  // open: en
endmodule
