// Logisim project 2-1 mux.circ as structural Verilog: 1 circuit, main circuit 2-1 mux
module _2_1_mux (
  input  x,
  input  y,
  input  s,
  output out_4
);

  wire and_1_out, and_2_out, not_1_out;

  not not_1 (not_1_out, s);
  and and_1 (and_1_out, x, not_1_out);
  and and_2 (and_2_out, y, s);
  or or_1 (out_4, and_1_out, and_2_out);
endmodule
