// Logisim project brojac 0-9.circ as structural Verilog: 1 circuit, main circuit brojac 0-9
module brojac_0_9 (
);

  wire A_qn, and_1_out, and_2_out, and_3_out, B_q, C_q, clock_out, D_q;

  Clock clock (.out(clock_out));
  and and_1 (and_1_out, A_qn, D_q);
  J_K_Flip_Flop D (.J(1'b1), .clk(clock_out), .K(1'b1), .Q(D_q));  // open: Qn, preset, en, reset
  J_K_Flip_Flop C (.J(and_1_out), .clk(clock_out), .K(D_q), .Q(C_q));  // open: Qn, preset, en, reset
  and and_2 (and_2_out, D_q, C_q);
  J_K_Flip_Flop B (.J(and_2_out), .clk(clock_out), .K(and_2_out), .Q(B_q));  // open: Qn, preset, en, reset
  and and_3 (and_3_out, and_2_out, B_q);
  J_K_Flip_Flop A (.J(and_3_out), .clk(clock_out), .K(D_q), .Qn(A_qn));  // open: Q, preset, en, reset
endmodule
