// Logisim project 3.circ as structural Verilog: 1 circuit, main circuit 3
module _3 (
  input  in_1,
  input  in_2,
  input  in_3,
  input  in_4,
  input  in_5,
  input  in_6,
  output out_7
);

  wire multiplexer_1_out, multiplexer_2_out, multiplexer_3_out, multiplexer_4_out, x0_q, x1_q, x2_q;

  Multiplexer multiplexer_1 (.in0(in_3), .in1(x1_q), .out(multiplexer_1_out), .sel(in_2));  // open: en
  D_Flip_Flop x0 (.clk(in_1), .D(multiplexer_1_out), .Q(x0_q));  // open: Qn, preset, en, reset
  D_Flip_Flop x1 (.clk(in_1), .D(multiplexer_2_out), .Q(x1_q));  // open: Qn, preset, en, reset
  Multiplexer multiplexer_2 (.in0(in_4), .in1(x2_q), .out(multiplexer_2_out), .sel(in_2));  // open: en
  Multiplexer multiplexer_3 (.in0(in_5), .in1(out_7), .out(multiplexer_3_out), .sel(in_2));  // open: en
  D_Flip_Flop x2 (.clk(in_1), .D(multiplexer_3_out), .Q(x2_q));  // open: Qn, preset, en, reset
  D_Flip_Flop x3 (.clk(in_1), .D(multiplexer_4_out), .Q(out_7));  // open: Qn, preset, en, reset
  Multiplexer multiplexer_4 (.in0(in_6), .in1(x0_q), .out(multiplexer_4_out), .sel(in_2));  // open: en
endmodule
