// Logisim project 5.circ as structural Verilog: 1 circuit, main circuit 5
module _5 (
  input  in_1,
  input  S_in,
  input  [1:0] C,
  output out_4
);

  wire multiplexer_1_out, multiplexer_2_out, multiplexer_3_out, multiplexer_4_out, x0_q, x0_qn, x1_q, x1_qn,
       x2_q, x2_qn, x3_qn;

  Multiplexer #(.select(2)) multiplexer_1 (
    .in0(S_in), .in1(x0_qn), .in2(x1_q), .in3(1'b0), .out(multiplexer_1_out), .sel(C));  // open: en
  D_Flip_Flop x0 (.clk(in_1), .D(multiplexer_1_out), .Q(x0_q), .Qn(x0_qn));  // open: preset, en, reset
  Multiplexer #(.select(2)) multiplexer_2 (
    .in0(x0_q), .in1(x1_qn), .in2(x2_q), .in3(1'b0), .out(multiplexer_2_out), .sel(C));  // open: en
  D_Flip_Flop x1 (.clk(in_1), .D(multiplexer_2_out), .Q(x1_q), .Qn(x1_qn));  // open: preset, en, reset
  Multiplexer #(.select(2)) multiplexer_3 (
    .in0(x1_q), .in1(x2_qn), .in2(out_4), .in3(1'b0), .out(multiplexer_3_out), .sel(C));  // open: en
  D_Flip_Flop x2 (.clk(in_1), .D(multiplexer_3_out), .Q(x2_q), .Qn(x2_qn));  // open: preset, en, reset
  Multiplexer #(.select(2)) multiplexer_4 (
    .in0(x2_q), .in1(x3_qn), .in2(x0_q), .in3(1'b0), .out(multiplexer_4_out), .sel(C));  // open: en
  D_Flip_Flop x3 (.clk(in_1), .D(multiplexer_4_out), .Q(out_4), .Qn(x3_qn));  // open: preset, en, reset
endmodule
