// Logisim project 7.circ as structural Verilog: 1 circuit, main circuit 7
module _7 (
  input  in_1,
  input  S_in,
  input  in_3,
  input  in_4,
  input  in_5,
  input  in_6,
  output out_7
);

  wire d_ff_1_q, d_ff_2_q, multiplexer_1_out, multiplexer_2_out, multiplexer_3_out;

  Multiplexer multiplexer_1 (.in0(S_in), .in1(in_4), .out(multiplexer_1_out), .sel(in_3));  // open: en
  D_Flip_Flop d_ff_1 (.clk(in_1), .D(multiplexer_1_out), .Q(d_ff_1_q));  // open: Qn, preset, en, reset
  D_Flip_Flop d_ff_2 (.clk(in_1), .D(multiplexer_2_out), .Q(d_ff_2_q));  // open: Qn, preset, en, reset
  Multiplexer multiplexer_2 (.in0(d_ff_1_q), .in1(in_5), .out(multiplexer_2_out), .sel(in_3));  // open: en
  Multiplexer multiplexer_3 (.in0(d_ff_2_q), .in1(in_6), .out(multiplexer_3_out), .sel(in_3));  // open: en
  D_Flip_Flop d_ff_3 (.clk(in_1), .D(multiplexer_3_out), .Q(out_7));  // open: Qn, preset, en, reset
endmodule
