// Logisim project 8.circ as structural Verilog: 1 circuit, main circuit main
module main (
);

  wire and_1_out, and_2_out, and_3_out, B_q, B_qn, C_q, clock_1_out, D_q;

  Clock clock_1 (.out(clock_1_out));
  J_K_Flip_Flop D (.J(1'b1), .clk(clock_1_out), .K(1'b1), .Q(D_q));  // open: Qn, preset, en, reset
  and and_1 (and_1_out, B_qn, D_q);
  J_K_Flip_Flop C (.J(and_1_out), .clk(clock_1_out), .K(D_q), .Q(C_q));  // open: Qn, preset, en, reset
  and and_2 (and_2_out, D_q, C_q);
  J_K_Flip_Flop B (.J(and_2_out), .clk(clock_1_out), .K(D_q), .Q(B_q), .Qn(B_qn));  // open: preset, en, reset
  and and_3 (and_3_out, D_q, B_q);
  J_K_Flip_Flop A (.J(and_3_out), .clk(clock_1_out), .K(and_3_out));  // open: Q, Qn, preset, en, reset
endmodule
