// Logisim project brojac 0-15.circ as structural Verilog: 1 circuit, main circuit brojac 0-15
module brojac_0_15 (
);

  wire and_1_out, and_2_out, B_q, C_q, clock_1_out, D_q;

  Clock clock_1 (.out(clock_1_out));
  J_K_Flip_Flop D (.J(1'b1), .clk(clock_1_out), .K(1'b1), .Q(D_q));  // open: Qn, preset, en, reset
  J_K_Flip_Flop C (.J(D_q), .clk(clock_1_out), .K(D_q), .Q(C_q));  // open: Qn, preset, en, reset
  and and_1 (and_1_out, D_q, C_q);
  J_K_Flip_Flop B (.J(and_1_out), .clk(clock_1_out), .K(and_1_out), .Q(B_q));  // open: Qn, preset, en, reset
  and and_2 (and_2_out, and_1_out, B_q);
  J_K_Flip_Flop A (.J(and_2_out), .clk(clock_1_out), .K(and_2_out));  // open: Q, Qn, preset, en, reset
endmodule
