// Logisim project brojac 0-2-3-6-4-1.circ as structural Verilog: 1 circuit, main circuit brojac 0-2-3-6-4-1
module brojac_0_2_3_6_4_1 (
);

  wire A_q, A_qn, and_1_out, and_2_out, B_q, B_qn, C_q, C_qn, clock_out, xor_1_out;

  Clock clock (.out(clock_out));
  J_K_Flip_Flop C (.J(xor_1_out), .clk(clock_out), .K(1'b1), .Q(C_q), .Qn(C_qn));  // open: preset, en, reset
  xor xor_1 (xor_1_out, B_q, A_q);
  and and_1 (and_1_out, A_qn, C_qn);
  J_K_Flip_Flop B (.J(and_1_out), .clk(clock_out), .K(A_q), .Q(B_q), .Qn(B_qn));  // open: preset, en, reset
  and and_2 (and_2_out, C_q, B_q);
  J_K_Flip_Flop A (.J(and_2_out), .clk(clock_out), .K(B_qn), .Q(A_q), .Qn(A_qn));  // open: preset, en, reset
endmodule
