// Logisim project brojac 0-2-5-3.circ as structural Verilog: 1 circuit, main circuit brojac 0-2-5-3
module brojac_0_2_5_3 (
);

  wire and_1_out, B_q, C_qn, clock_1_out;

  and and_1 (and_1_out, C_qn, B_q);
  J_K_Flip_Flop A (.J(and_1_out), .clk(clock_1_out), .K(1'b1));  // open: Q, Qn, preset, en, reset
  J_K_Flip_Flop B (.J(1'b1), .clk(clock_1_out), .K(1'b1), .Q(B_q));  // open: Qn, preset, en, reset
  J_K_Flip_Flop C (.J(B_q), .clk(clock_1_out), .K(B_q), .Qn(C_qn));  // open: Q, preset, en, reset
  Clock clock_1 (.out(clock_1_out));
endmodule
