// Logisim project funkcija iz tabele 2.circ as structural Verilog: 1 circuit, main circuit funkcija iz tabele 2
module funkcija_iz_tabele_2 (
  input  D,
  input  [2:0] in_2,
  output out_3
);

  wire not_1_out;

  not not_1 (not_1_out, D);
  Multiplexer #(.select(3)) multiplexer_1 (
    .in0(1'b0), .in1(D), .in2(1'b1), .in3(not_1_out), .in4(1'b1), .in5(D), .in6(D), .in7(1'b0), .out(out_3),
    .sel(in_2));  // open: en
endmodule
