// Logisim project funkcija iz tabele.circ as structural Verilog: 1 circuit, main circuit funkcija iz tabele
module funkcija_iz_tabele (
  input  D,
  input  [2:0] in_2,
  output out_3
);

  wire not_1_out;

  not not_1 (not_1_out, D);
  Multiplexer #(.select(3)) multiplexer_1 (
    .in0(D), .in1(1'b0), .in2(1'b1), .in3(1'b0), .in4(not_1_out), .in5(1'b1), .in6(not_1_out), .in7(D),
    .out(out_3), .sel(in_2));  // open: en
endmodule
