// Logisim project logicki izrazi.circ as structural Verilog: 1 circuit, main circuit logicki izrazi
module logicki_izrazi (
  input  x0,
  input  y0,
  input  x1,
  input  y1,
  input  x2,
  input  y2,
  input  x3,
  input  y3,
  input  [1:0] in_9,
  output out_10,
  output out_11,
  output out_12,
  output out_13
);

  wire and_1_out, and_2_out, and_3_out, and_4_out, not_1_out, not_2_out, not_3_out, not_4_out, or_1_out,
       or_2_out, or_3_out, or_4_out, xor_1_out, xor_2_out, xor_3_out, xor_4_out;

  and and_1 (and_1_out, x0, y0);
  or or_1 (or_1_out, x0, y0);
  Multiplexer #(.select(2)) multiplexer_1 (
    .in0(and_1_out), .in1(or_1_out), .in2(xor_1_out), .in3(not_1_out), .out(out_10), .sel(in_9));  // open: en
  not not_1 (not_1_out, x0);
  xor xor_1 (xor_1_out, x0, y0);
  and and_2 (and_2_out, x1, y1);
  or or_2 (or_2_out, x1, y1);
  xor xor_2 (xor_2_out, x1, y1);
  Multiplexer #(.select(2)) multiplexer_2 (
    .in0(and_2_out), .in1(or_2_out), .in2(xor_2_out), .in3(not_2_out), .out(out_11), .sel(in_9));  // open: en
  not not_2 (not_2_out, x1);
  and and_3 (and_3_out, x2, y2);
  or or_3 (or_3_out, x2, y2);
  Multiplexer #(.select(2)) multiplexer_3 (
    .in0(and_3_out), .in1(or_3_out), .in2(xor_3_out), .in3(not_3_out), .out(out_12), .sel(in_9));  // open: en
  not not_3 (not_3_out, x2);
  xor xor_3 (xor_3_out, x2, y2);
  and and_4 (and_4_out, x3, y3);
  or or_4 (or_4_out, x3, y3);
  xor xor_4 (xor_4_out, x3, y3);
  Multiplexer #(.select(2)) multiplexer_4 (
    .in0(and_4_out), .in1(or_4_out), .in2(xor_4_out), .in3(not_4_out), .out(out_13), .sel(in_9));  // open: en
  not not_4 (not_4_out, x3);
endmodule
