// Logisim project pomeracki registar.circ as structural Verilog: 1 circuit, main circuit pomeracki registar
module pomeracki_registar (
  input  in_1,
  input  S_in,
  input  [1:0] S,
  input  p0,
  input  p1,
  input  p2,
  input  p3,
  input  p4,
  input  p5,
  output S_out
);

  wire multiplexer_1_out, multiplexer_2_out, multiplexer_3_out, multiplexer_4_out, multiplexer_5_out,
       multiplexer_6_out, x0_q, x0_qn, x1_q, x1_qn, x2_q, x2_qn, x3_q, x3_qn, x4_q, x4_qn, x5_qn;

  Multiplexer #(.select(2)) multiplexer_1 (
    .in0(p0), .in1(x2_q), .in2(x0_qn), .in3(S_in), .out(multiplexer_1_out), .sel(S));  // open: en
  D_Flip_Flop x0 (.clk(in_1), .D(multiplexer_1_out), .Q(x0_q), .Qn(x0_qn));  // open: preset, en, reset
  Multiplexer #(.select(2)) multiplexer_2 (
    .in0(p1), .in1(x3_q), .in2(x1_qn), .in3(x0_q), .out(multiplexer_2_out), .sel(S));  // open: en
  D_Flip_Flop x1 (.clk(in_1), .D(multiplexer_2_out), .Q(x1_q), .Qn(x1_qn));  // open: preset, en, reset
  Multiplexer #(.select(2)) multiplexer_3 (
    .in0(p2), .in1(x4_q), .in2(x2_qn), .in3(x1_q), .out(multiplexer_3_out), .sel(S));  // open: en
  D_Flip_Flop x2 (.clk(in_1), .D(multiplexer_3_out), .Q(x2_q), .Qn(x2_qn));  // open: preset, en, reset
  D_Flip_Flop x3 (.clk(in_1), .D(multiplexer_4_out), .Q(x3_q), .Qn(x3_qn));  // open: preset, en, reset
  Multiplexer #(.select(2)) multiplexer_4 (
    .in0(p3), .in1(multiplexer_6_out), .in2(x3_qn), .in3(x2_q), .out(multiplexer_4_out), .sel(S));  // open: en
  Multiplexer #(.select(2)) multiplexer_5 (
    .in0(p4), .in1(x0_q), .in2(x4_qn), .in3(x3_q), .out(multiplexer_5_out), .sel(S));  // open: en
  D_Flip_Flop x4 (.clk(in_1), .D(multiplexer_5_out), .Q(x4_q), .Qn(x4_qn));  // open: preset, en, reset
  Multiplexer #(.select(2)) multiplexer_6 (
    .in0(p5), .in1(x1_q), .in2(x5_qn), .in3(x4_q), .out(multiplexer_6_out), .sel(S));  // open: en
  D_Flip_Flop x5 (.clk(in_1), .D(multiplexer_6_out), .Q(S_out), .Qn(x5_qn));  // open: preset, en, reset
endmodule
