// Logisim project serijski i paralelni ulaz.circ as structural Verilog: 1 circuit, main circuit serijski i paralelni ulaz
module serijski_i_paralelni_ulaz (
  input  in_1,
  input  S_in,
  input  paralel,
  input  p0,
  input  p1,
  input  p2,
  input  p3,
  output S_out
);

  wire multiplexer_1_out, multiplexer_2_out, multiplexer_3_out, multiplexer_4_out, x0_q, x1_q, x2_q;

  D_Flip_Flop x0 (.clk(in_1), .D(multiplexer_1_out), .Q(x0_q));  // open: Qn, preset, en, reset
  Multiplexer multiplexer_1 (.in0(S_in), .in1(p0), .out(multiplexer_1_out), .sel(paralel));  // open: en
  Multiplexer multiplexer_2 (.in0(x0_q), .in1(p1), .out(multiplexer_2_out), .sel(paralel));  // open: en
  D_Flip_Flop x1 (.clk(in_1), .D(multiplexer_2_out), .Q(x1_q));  // open: Qn, preset, en, reset
  Multiplexer multiplexer_3 (.in0(x1_q), .in1(p2), .out(multiplexer_3_out), .sel(paralel));  // open: en
  D_Flip_Flop x2 (.clk(in_1), .D(multiplexer_3_out), .Q(x2_q));  // open: Qn, preset, en, reset
  Multiplexer multiplexer_4 (.in0(x2_q), .in1(p3), .out(multiplexer_4_out), .sel(paralel));  // open: en
  D_Flip_Flop x3 (.clk(in_1), .D(multiplexer_4_out), .Q(S_out));  // open: Qn, preset, en, reset
endmodule
